// Logisim project Parte 3 - Projeto - Linsmar.circ as structural Verilog: 9 circuits, main circuit Junção ULA com Reg
module \Junção_ULA_com_Reg  (
  input  [3:0] in_1,
  input  [7:0] in_2,
  output [7:0] RX,
  output [7:0] RY
);

  wire clock_1_out, clock_2_out, demultiplexer_1_out10, demultiplexer_1_out12, multiplexer_3_out, R0,
       RM_WM_ctl, RWctl;
  wire [1:0] ctlu_1_rdctl, PCctl;
  wire [2:0] RINctl;
  wire [3:0] Operador, RDctl, RX_RS1, RY_RS2;
  wire [7:0] multiplexer_2_out, Saida_8bit, Saida_ULA, SaidaPC, SaidaRAM;
  wire [11:0] rom_1_data, Saida_IR;

  IDEC IDEC (.Operador(Operador), .RX(RX_RS1), .RY(RY_RS2), ._12_bits_instru(Saida_IR), .Saida_8bit_IDEC(Saida_8bit));
  Multiplexer #(.select(2), .width(4)) multiplexer_1 (
    .in0(4'b0000), .in1(4'b1111), .in2(RX_RS1), .out(RDctl), .sel(ctlu_1_rdctl));  // open: in3, en
  CTLU ctlu_1 (
    .R0ctlu(R0), .RWctl(RWctl), .RINctl(RINctl), .PCctl(PCctl), .RDctl(ctlu_1_rdctl),
    .RMctl_WMctl(RM_WM_ctl), .in_1(Operador));
  Multiplexer #(.select(3), .width(8)) multiplexer_2 (
    .in0(Saida_ULA), .in1(SaidaRAM), .in2(Saida_8bit), .in3(RY), .in4(SaidaPC), .out(multiplexer_2_out),
    .sel(RINctl));  // open: in5, in6, in7, en
  Clock clock_1 (.out(clock_1_out));
  Registradores REGS (
    .Pino_R0(R0), .RIN(multiplexer_2_out), .RWctl(RWctl), .RX(RX), .RY(RY), .RD(RDctl), .RS1(RX_RS1),
    .RS2(RY_RS2));
  Multiplexer #(.select(2)) multiplexer_3 (
    .in1(clock_1_out), .in2(1'b1), .out(multiplexer_3_out), .sel(PCctl));  // open: in0, in3, en
  Demultiplexer #(.select(4)) demultiplexer_1 (
    .out10(demultiplexer_1_out10), .out12(demultiplexer_1_out12), .in(RM_WM_ctl), .sel(Operador));  // open: out0, out1, out2, out3, out4, out5, out6, out7, out8, out9, out11, out13, out14, out15, en
  ULA ULA (.Saida_da_ULA(Saida_ULA), .Entrada_ULA_1(RX), .Entrada_ULA_2(RY), .Seletor_ULA(Operador));
  Counter #(.trigger("falling")) PC (
    .count(multiplexer_3_out), .Q(SaidaPC), .clk(clock_2_out));  // open: load, D, carry, clr
  Register #(.width(12)) IR (.D(rom_1_data), .Q(Saida_IR), .clk(clock_2_out));  // open: en, clr
  ROM #(.dataWidth(12)) rom_1 (.addr(SaidaPC), .data(rom_1_data));  // open: sel
  RAM #(.bus("separate")) ram_1 (
    .addr(in_2), .din(RX), .data(SaidaRAM), .str(demultiplexer_1_out12), .clk(clock_2_out),
    .ld(demultiplexer_1_out10));  // open: sel, clr
  Clock clock_2 (.out(clock_2_out));

  // Other names for the same wires on the sheet: SaidaREGforCTLU[7:0] = RX; SaidaREGforCTLURY[7:0] = RY

  // Notes on the sheet:
  //   IM
  //   DM
  //   contents of rom_1 (hex, n*v repeats v):
  //   b00 d10 b0a d20 b01 d30 812 200 e0d 331 d10 b01 e06 d01 c00 f00
endmodule

module ULA (
  input  [7:0] Entrada_ULA_1,
  input  [7:0] Entrada_ULA_2,
  input  [3:0] Seletor_ULA,
  output [7:0] Saida_da_ULA
);

  wire comparator_1_eq, comparator_2_lt, comparator_3_eq, comparator_3_lt, NOR_out_2, or_2_out;
  wire [7:0] adder_1_out, and_1_out, bit_extender_1_out, bit_extender_2_out, bit_extender_3_out,
       bit_extender_4_out, divider_1_out, multiplier_1_out, or_1_out, subtractor_1_out;

  assign and_1_out = Entrada_ULA_1 & Entrada_ULA_2;  // AND_Gate and_1, 8 bits wide
  assign or_1_out = Entrada_ULA_2 | Entrada_ULA_1;  // OR_Gate or_1, 8 bits wide
  Porta_NOR_da_ULA NOR (.in_1(Entrada_ULA_1), .out_2(NOR_out_2));
  Adder adder_1 (.a(Entrada_ULA_1), .b(Entrada_ULA_2), .out(adder_1_out));  // open: cin, cout
  Subtractor subtractor_1 (.a(Entrada_ULA_1), .b(Entrada_ULA_2), .out(subtractor_1_out));  // open: bin, bout
  Multiplier multiplier_1 (.a(Entrada_ULA_1), .b(Entrada_ULA_2), .out(multiplier_1_out));  // open: cin, cout
  Divider divider_1 (.a(Entrada_ULA_1), .b(Entrada_ULA_2), .out(divider_1_out));  // open: upper, rem
  Comparator #(.mode("unsigned")) comparator_1 (
    .a(Entrada_ULA_1), .b(Entrada_ULA_2), .eq(comparator_1_eq));  // open: gt, lt
  Comparator #(.mode("unsigned")) comparator_2 (
    .a(Entrada_ULA_1), .b(Entrada_ULA_2), .lt(comparator_2_lt));  // open: gt, eq
  Comparator #(.mode("unsigned")) comparator_3 (
    .a(Entrada_ULA_1), .b(Entrada_ULA_2), .eq(comparator_3_eq), .lt(comparator_3_lt));  // open: gt
  assign bit_extender_1_out = {{7{1'b0}}, NOR_out_2};  // Bit_Extender bit_extender_1
  assign bit_extender_2_out = {{7{1'b0}}, comparator_1_eq};  // Bit_Extender bit_extender_2
  assign bit_extender_3_out = {{7{1'b0}}, comparator_2_lt};  // Bit_Extender bit_extender_3
  assign bit_extender_4_out = {{7{1'b0}}, or_2_out};  // Bit_Extender bit_extender_4
  or or_2 (or_2_out, comparator_3_eq, comparator_3_lt);
  Multiplexer #(.select(4), .width(8), .enable("false")) multiplexer_1 (
    .in0(and_1_out), .in1(or_1_out), .in2(bit_extender_1_out), .in3(adder_1_out), .in4(subtractor_1_out),
    .in5(multiplier_1_out), .in6(divider_1_out), .in7(bit_extender_2_out), .in8(bit_extender_3_out),
    .in9(bit_extender_4_out), .out(Saida_da_ULA), .sel(Seletor_ULA));  // open: in10, in11, in12, in13, in14, in15

  // Notes on the sheet:
  //   Código
  //   Operação
  //   00
  //   E bit-a-bit
  //   01
  //   OU bit-a-bit
  //   02
  //   Não lógico
  //   03
  //   Adição
  //   04
  //   Subtração
  //   05
  //   06
  //   Divisão
  //   07
  //   Igual
  //   08
  //   Menor
  //   09
  //   Multiplicação
  //   Menor ou igual
endmodule

module Porta_NOR_da_ULA (
  input  [7:0] in_1,
  output out_2
);

  and and_1 (out_2, ~in_1[0], ~in_1[1], ~in_1[2], ~in_1[3], ~in_1[4], ~in_1[5], ~in_1[6], ~in_1[7]);  // AND_Gate
endmodule

module Registradores (
  input  [7:0] RIN,
  input  RWctl,
  input  [3:0] RD,
  input  [3:0] RS1,
  input  [3:0] RS2,
  output Pino_R0,
  output [7:0] RX,
  output [7:0] RY
);

  wire clock_1_out, demultiplexer_1_out0, demultiplexer_1_out1, demultiplexer_1_out2, demultiplexer_1_out3,
       demultiplexer_1_out4, demultiplexer_1_out5, demultiplexer_1_out6, demultiplexer_1_out7,
       demultiplexer_1_out8, demultiplexer_1_out9, demultiplexer_1_out10, demultiplexer_1_out11,
       demultiplexer_1_out12, demultiplexer_1_out13, demultiplexer_1_out14, demultiplexer_1_out15, not_1_out;
  wire [7:0] R0, R1, R2, R3, R4, R5, R6, R7, R8, R9, R10, R11, R12, R13, R14, R15;

  _0_ou_1_R0 u_0_ou_1_r0_1 (.Entrada_0_OU_1(R0), .\Saída_0_OU_1 (Pino_R0));
  Clock clock_1 (.out(clock_1_out));
  Demultiplexer #(.select(4)) demultiplexer_1 (
    .out0(demultiplexer_1_out0), .out1(demultiplexer_1_out1), .out2(demultiplexer_1_out2),
    .out3(demultiplexer_1_out3), .out4(demultiplexer_1_out4), .out5(demultiplexer_1_out5),
    .out6(demultiplexer_1_out6), .out7(demultiplexer_1_out7), .out8(demultiplexer_1_out8),
    .out9(demultiplexer_1_out9), .out10(demultiplexer_1_out10), .out11(demultiplexer_1_out11),
    .out12(demultiplexer_1_out12), .out13(demultiplexer_1_out13), .out14(demultiplexer_1_out14),
    .out15(demultiplexer_1_out15), .in(not_1_out), .sel(RD));  // open: en
  not not_1 (not_1_out, RWctl);
  Register register_1 (.D(RIN), .en(demultiplexer_1_out0), .Q(R0), .clk(clock_1_out));  // open: clr
  Register register_2 (.D(RIN), .en(demultiplexer_1_out1), .Q(R1), .clk(clock_1_out));  // open: clr
  Register register_3 (.D(RIN), .en(demultiplexer_1_out2), .Q(R2), .clk(clock_1_out));  // open: clr
  Register register_4 (.D(RIN), .en(demultiplexer_1_out4), .Q(R4), .clk(clock_1_out));  // open: clr
  Register register_5 (.D(RIN), .en(demultiplexer_1_out3), .Q(R3), .clk(clock_1_out));  // open: clr
  Register register_6 (.D(RIN), .en(demultiplexer_1_out5), .Q(R5), .clk(clock_1_out));  // open: clr
  Register register_7 (.D(RIN), .en(demultiplexer_1_out6), .Q(R6), .clk(clock_1_out));  // open: clr
  Multiplexer #(.select(4), .width(8)) multiplexer_1 (
    .in0(R0), .in1(R1), .in2(R2), .in3(R3), .in4(R4), .in5(R5), .in6(R6), .in7(R7), .in8(R8), .in9(R9),
    .in10(R10), .in11(R11), .in12(R12), .in13(R13), .in14(R14), .in15(R15), .out(RX), .sel(RS1));  // open: en
  Multiplexer #(.select(4), .width(8)) multiplexer_2 (
    .in0(R0), .in1(R1), .in2(R2), .in3(R3), .in4(R4), .in5(R5), .in6(R6), .in7(R7), .in8(R8), .in9(R9),
    .in10(R10), .in11(R11), .in12(R12), .in13(R13), .in14(R14), .in15(R15), .out(RY), .sel(RS2));  // open: en
  Register register_8 (.D(RIN), .en(demultiplexer_1_out7), .Q(R7), .clk(clock_1_out));  // open: clr
  Register register_9 (.D(RIN), .en(demultiplexer_1_out8), .Q(R8), .clk(clock_1_out));  // open: clr
  Register register_10 (.D(RIN), .en(demultiplexer_1_out9), .Q(R9), .clk(clock_1_out));  // open: clr
  Register register_11 (.D(RIN), .en(demultiplexer_1_out10), .Q(R10), .clk(clock_1_out));  // open: clr
  Register register_12 (.D(RIN), .en(demultiplexer_1_out11), .Q(R11), .clk(clock_1_out));  // open: clr
  Register register_13 (.D(RIN), .en(demultiplexer_1_out13), .Q(R13), .clk(clock_1_out));  // open: clr
  Register register_14 (.D(RIN), .en(demultiplexer_1_out12), .Q(R12), .clk(clock_1_out));  // open: clr
  Register register_15 (.D(RIN), .en(demultiplexer_1_out14), .Q(R14), .clk(clock_1_out));  // open: clr
  Register register_16 (.D(RIN), .en(demultiplexer_1_out15), .Q(R15), .clk(clock_1_out));  // open: clr
endmodule

module _0_ou_1_R0 (
  input  [7:0] Entrada_0_OU_1,
  output \Saída_0_OU_1 
);

  or or_1 (\Saída_0_OU_1 , Entrada_0_OU_1[0], Entrada_0_OU_1[1], Entrada_0_OU_1[2], Entrada_0_OU_1[3], Entrada_0_OU_1[4], Entrada_0_OU_1[5], Entrada_0_OU_1[6], Entrada_0_OU_1[7]);
endmodule

module CTLU (
  input  [3:0] in_1,
  input  R0ctlu,
  output RWctl,
  output [2:0] RINctl,
  output [1:0] PCctl,
  output [1:0] RDctl,
  output RMctl_WMctl
);

  Comparator #(.width(4)) comparator_1 (.a(in_1), .b(4'b1100), .eq(RWctl));  // open: gt, lt
  Multiplexer #(.select(4), .width(3)) multiplexer_1 (
    .in0(3'b000), .in1(3'b000), .in2(3'b000), .in3(3'b000), .in4(3'b000), .in5(3'b000), .in6(3'b000),
    .in7(3'b000), .in8(3'b000), .in9(3'b000), .in10(3'b001), .in11(3'b010), .in12(3'b000), .in13(3'b011),
    .in14(3'b100), .in15(3'b111), .out(RINctl), .sel(in_1));  // open: en
  Multiplexer #(.select(4), .width(2)) multiplexer_2 (
    .in0(2'b00), .in1(2'b00), .in2(2'b00), .in3(2'b00), .in4(2'b00), .in5(2'b00), .in6(2'b00), .in7(2'b00),
    .in8(2'b00), .in9(2'b00), .in10(2'b00), .in11(2'b00), .in12(2'b10), .in13(2'b10), .in14(2'b01),
    .in15(2'b01), .out(RDctl), .sel(in_1));  // open: en
  Multiplexer #(.select(4)) multiplexer_3 (
    .in0(1'b0), .in1(1'b0), .in2(1'b0), .in3(1'b0), .in4(1'b0), .in5(1'b0), .in6(1'b0), .in7(1'b0),
    .in8(1'b0), .in9(1'b0), .in10(1'b1), .in11(1'b0), .in12(1'b1), .in13(1'b0), .in14(1'b0), .in15(1'b0),
    .out(RMctl_WMctl), .sel(in_1));  // open: en
  PCctl pcctl_1 (.Ope(in_1), .R0(R0ctlu), .PCctl(PCctl));

  // Other names for the same wires on the sheet: Op[3:0] = in_1
endmodule

module PCctl (
  input  [3:0] Ope,
  input  R0,
  output [1:0] PCctl
);

  wire and_2_out, and_3_out;

  and and_1 (PCctl[1], ~Ope[0], Ope[1], Ope[2], Ope[3], R0);  // AND_Gate
  and and_2 (and_2_out, ~Ope[0], Ope[1], Ope[2], Ope[3], ~R0);  // AND_Gate
  and and_3 (and_3_out, ~Ope[1], Ope[2], Ope[3]);  // AND_Gate
  or or_1 (PCctl[0], and_2_out, ~Ope[2], ~Ope[3], and_3_out);  // OR_Gate
endmodule

module IDEC (
  input  [11:0] _12_bits_instru,
  output [3:0] Operador,
  output [3:0] RX,
  output [3:0] RY,
  output [7:0] Saida_8bit_IDEC
);


  assign Operador = _12_bits_instru[11:8];
  assign RX = _12_bits_instru[7:4];
  assign RY = _12_bits_instru[3:0];
  assign Saida_8bit_IDEC = _12_bits_instru[7:0];
endmodule

module Testes (
  input  [11:0] in_1,
  output [11:0] out_2
);

  wire [11:0] rom_1_data;

  ROM #(.dataWidth(12)) rom_1 (.data(rom_1_data));  // open: addr, sel
  RAM #(.bus("separate")) ram_1 ();  // open: addr, din, data, str, sel, clk, ld, clr

  assign out_2 = in_1;

  // Notes on the sheet:
  //   IM
  //   DM
  //   Jesus cristo essa parte 3 bixo
endmodule
