// Logisim project lista4.circ as structural Verilog: 5 circuits, main circuit 12
module _4 (
  output out_1,
  output out_2,
  output out_3,
  output out_4
);

  wire and_1_out, clock_1_out, t_ff_1_qn, t_ff_2_qn, t_ff_3_qn, t_ff_4_qn;

  Clock clock_1 (.out(clock_1_out));
  T_Flip_Flop #(.trigger("falling")) t_ff_1 (
    .clk(clock_1_out), .T(1'b1), .Q(out_1), .Qn(t_ff_1_qn), .reset(and_1_out));  // open: preset, en
  T_Flip_Flop #(.trigger("falling")) t_ff_2 (
    .clk(out_1), .T(1'b1), .Q(out_2), .Qn(t_ff_2_qn), .reset(and_1_out));  // open: preset, en
  T_Flip_Flop #(.trigger("falling")) t_ff_3 (
    .clk(out_2), .T(1'b1), .Q(out_3), .Qn(t_ff_3_qn), .reset(and_1_out));  // open: preset, en
  T_Flip_Flop #(.trigger("falling")) t_ff_4 (
    .clk(out_3), .T(1'b1), .Q(out_4), .Qn(t_ff_4_qn), .reset(and_1_out));  // open: preset, en
  and and_1 (and_1_out, ~t_ff_1_qn, ~t_ff_2_qn, t_ff_3_qn, ~t_ff_4_qn);  // AND_Gate
endmodule

module _5 (
  output out_1,
  output out_2,
  output out_3,
  output out_4
);

  wire and_1_out, clock_1_out, t_ff_1_qn, t_ff_2_qn, t_ff_3_qn, t_ff_4_qn;

  Clock clock_1 (.out(clock_1_out));
  T_Flip_Flop #(.trigger("falling")) t_ff_1 (
    .clk(clock_1_out), .T(1'b1), .Q(out_1), .Qn(t_ff_1_qn), .reset(and_1_out));  // open: preset, en
  T_Flip_Flop #(.trigger("falling")) t_ff_2 (
    .clk(out_1), .T(1'b1), .Q(out_2), .Qn(t_ff_2_qn), .reset(and_1_out));  // open: preset, en
  T_Flip_Flop #(.trigger("falling")) t_ff_3 (
    .clk(out_2), .T(1'b1), .Q(out_3), .Qn(t_ff_3_qn), .reset(and_1_out));  // open: preset, en
  T_Flip_Flop #(.trigger("falling")) t_ff_4 (
    .clk(out_3), .T(1'b1), .Q(out_4), .Qn(t_ff_4_qn), .reset(and_1_out));  // open: preset, en
  and and_1 (and_1_out, ~t_ff_1_qn, ~t_ff_2_qn, t_ff_3_qn, ~t_ff_4_qn);  // AND_Gate
endmodule

module johson (
  output [3:0] out_1,
  output out_2,
  output out_3,
  output out_4,
  output out_5
);

  wire clock_1_out, j_k_ff_1_qn, j_k_ff_2_qn, j_k_ff_3_qn, j_k_ff_4_qn;

  Clock clock_1 (.out(clock_1_out));
  J_K_Flip_Flop #(.trigger("falling")) j_k_ff_1 (
    .J(j_k_ff_4_qn), .clk(clock_1_out), .K(out_1[3]), .Q(out_1[0]), .Qn(j_k_ff_1_qn));  // open: preset, en, reset
  J_K_Flip_Flop #(.trigger("falling")) j_k_ff_2 (
    .J(out_1[0]), .clk(clock_1_out), .K(j_k_ff_1_qn), .Q(out_1[1]), .Qn(j_k_ff_2_qn));  // open: preset, en, reset
  J_K_Flip_Flop #(.trigger("falling")) j_k_ff_3 (
    .J(out_1[1]), .clk(clock_1_out), .K(j_k_ff_2_qn), .Q(out_1[2]), .Qn(j_k_ff_3_qn));  // open: preset, en, reset
  J_K_Flip_Flop #(.trigger("falling")) j_k_ff_4 (
    .J(out_1[2]), .clk(clock_1_out), .K(j_k_ff_3_qn), .Q(out_1[3]), .Qn(j_k_ff_4_qn));  // open: preset, en, reset

  assign out_2 = out_1[0];
  assign out_3 = out_1[1];
  assign out_4 = out_1[2];
  assign out_5 = out_1[3];
endmodule

module tipo_D_conversor_paralelo_serie (
  input  in_1,
  input  MODO_CARGA,
  input  CLEAR,
  input  EC3,
  input  EC2,
  input  EC1,
  input  EC0,
  output Q3,
  output Q2,
  output Q1,
  output Q0
);

  wire and_1_out, and_2_out, and_3_out, and_4_out, clock_1_out, not_1_out;

  Clock clock_1 (.out(clock_1_out));
  D_Flip_Flop #(.trigger("falling")) d_ff_1 (
    .clk(clock_1_out), .D(in_1), .Q(Q3), .preset(and_1_out), .reset(not_1_out));  // open: Qn, en
  and and_1 (and_1_out, MODO_CARGA, EC3);
  not not_1 (not_1_out, CLEAR);
  D_Flip_Flop #(.trigger("falling")) d_ff_2 (
    .clk(clock_1_out), .D(Q3), .Q(Q2), .preset(and_2_out), .reset(not_1_out));  // open: Qn, en
  and and_2 (and_2_out, MODO_CARGA, EC2);
  and and_3 (and_3_out, MODO_CARGA, EC1);
  D_Flip_Flop #(.trigger("falling")) d_ff_3 (
    .clk(clock_1_out), .D(Q2), .Q(Q1), .preset(and_3_out), .reset(not_1_out));  // open: Qn, en
  D_Flip_Flop #(.trigger("falling")) d_ff_4 (
    .clk(clock_1_out), .D(Q1), .Q(Q0), .preset(and_4_out), .reset(not_1_out));  // open: Qn, en
  and and_4 (and_4_out, MODO_CARGA, EC0);
endmodule

module _12 (
  input  [7:0] in_1,
  output [1:0] out_2
);

  wire demultiplexer_1_out0, demultiplexer_1_out1, demultiplexer_1_out2, demultiplexer_1_out3;

  Demultiplexer #(.select(2)) demultiplexer_1 (
    .out0(demultiplexer_1_out0), .out1(demultiplexer_1_out1), .out2(demultiplexer_1_out2),
    .out3(demultiplexer_1_out3), .in(1'b1), .sel(in_1[7:6]));  // open: en
  RAM #(.dataWidth(1), .bus("separate")) ram_1 (
    .addr(in_1), .sel(demultiplexer_1_out0));  // open: din, data, str, clk, ld, clr
  RAM #(.dataWidth(1), .bus("separate")) ram_2 (
    .addr(in_1), .sel(demultiplexer_1_out1));  // open: din, data, str, clk, ld, clr
  RAM #(.dataWidth(1), .bus("separate")) ram_3 (
    .addr(in_1), .sel(demultiplexer_1_out2));  // open: din, data, str, clk, ld, clr
  RAM #(.dataWidth(1), .bus("separate")) ram_4 (
    .addr(in_1), .sel(demultiplexer_1_out3));  // open: din, data, str, clk, ld, clr
  RAM #(.dataWidth(1), .bus("separate")) ram_5 (
    .addr(in_1), .sel(demultiplexer_1_out0));  // open: din, data, str, clk, ld, clr
  RAM #(.dataWidth(1), .bus("separate")) ram_6 (
    .addr(in_1), .sel(demultiplexer_1_out1));  // open: din, data, str, clk, ld, clr
  RAM #(.dataWidth(1), .bus("separate")) ram_7 (
    .addr(in_1), .sel(demultiplexer_1_out2));  // open: din, data, str, clk, ld, clr
  RAM #(.dataWidth(1), .bus("separate")) ram_8 (
    .addr(in_1), .sel(demultiplexer_1_out3));  // open: din, data, str, clk, ld, clr
  RAM #(.dataWidth(1), .bus("separate")) ram_9 (
    .addr(in_1), .sel(demultiplexer_1_out0));  // open: din, data, str, clk, ld, clr
  RAM #(.dataWidth(1), .bus("separate")) ram_10 (
    .addr(in_1), .sel(demultiplexer_1_out1));  // open: din, data, str, clk, ld, clr
  RAM #(.dataWidth(1), .bus("separate")) ram_11 (
    .addr(in_1), .sel(demultiplexer_1_out2));  // open: din, data, str, clk, ld, clr
  RAM #(.dataWidth(1), .bus("separate")) ram_12 (
    .addr(in_1), .sel(demultiplexer_1_out3));  // open: din, data, str, clk, ld, clr
  RAM #(.dataWidth(1), .bus("separate")) ram_13 (
    .addr(in_1), .sel(demultiplexer_1_out0));  // open: din, data, str, clk, ld, clr
  RAM #(.dataWidth(1), .bus("separate")) ram_14 (
    .addr(in_1), .sel(demultiplexer_1_out1));  // open: din, data, str, clk, ld, clr
  RAM #(.dataWidth(1), .bus("separate")) ram_15 (
    .addr(in_1), .sel(demultiplexer_1_out2));  // open: din, data, str, clk, ld, clr
  RAM #(.dataWidth(1), .bus("separate")) ram_16 (
    .addr(in_1), .sel(demultiplexer_1_out3));  // open: din, data, str, clk, ld, clr

  assign out_2 = in_1[7:6];
endmodule
